// Logisim project ALU_circuit.circ as structural Verilog: 4 circuits, main circuit main
module main (
  input  A4,
  input  A3,
  input  A2,
  input  A1,
  input  cs2,
  input  cs1,
  input  cs0,
  input  B4,
  input  B3,
  input  B2,
  input  B1,
  output V,
  output Z,
  output S,
  output C,
  output S4,
  output S3,
  output S2,
  output S1
);

  wire adapter_1_a_prime, adapter_1_cin, adapter_1_mux, adapter_1_s0, adapter_1_s1, adder_1_s1, adder_1_s2,
       adder_1_s3, adder_1_s4, fa_extender_1_b_2, fa_extender_2_b_2, fa_extender_3_b_2, fa_extender_4_b_2,
       n7408_1_p3, n7408_1_p6, n7408_1_p11, n7408_1_p14, n7432_1_p3, n7432_1_p6, n7432_1_p11, n7486_1_p3,
       n7486_1_p6, n7486_1_p11, n7486_1_p14;

  // _7408 7408_1: pin names not known; wires that end beside it: B1, A1, n7408_1_p3, B2, A2, n7408_1_p6, 1'b0, 1'b1, B3, A3, n7408_1_p11, B4, A4, n7408_1_p14
  Adapter adapter_1 (
    .MUX(adapter_1_mux), .s1(adapter_1_s1), .s0(adapter_1_s0), .A_prime(adapter_1_a_prime), .cs2(cs2),
    .cs1(cs1), .cs0(cs0), .Cin(adapter_1_cin));
  FA_Extender fa_extender_1 (.B(B1), .s1(adapter_1_s1), .s0(adapter_1_s0), .B_2(fa_extender_1_b_2));
  FA_Extender fa_extender_2 (.B(B2), .s1(adapter_1_s1), .s0(adapter_1_s0), .B_2(fa_extender_2_b_2));
  FA_Extender fa_extender_3 (.B(B3), .s1(adapter_1_s1), .s0(adapter_1_s0), .B_2(fa_extender_3_b_2));
  FA_Extender fa_extender_4 (.B(B4), .s1(adapter_1_s1), .s0(adapter_1_s0), .B_2(fa_extender_4_b_2));
  // _7486 7486_1: pin names not known; wires that end beside it: A4, adapter_1_a_prime, n7486_1_p3, A3, adapter_1_a_prime, n7486_1_p6, 1'b0, 1'b1, A1, adapter_1_a_prime, n7486_1_p11, A2, adapter_1_a_prime, n7486_1_p14
  Adder adder_1 (
    .A1(n7486_1_p11), .A2(n7486_1_p14), .A3(n7486_1_p6), .A4(n7486_1_p3), .B1(fa_extender_1_b_2),
    .B2(fa_extender_2_b_2), .B3(fa_extender_3_b_2), .B4(fa_extender_4_b_2), .Cout(C), .S1(adder_1_s1),
    .S2(adder_1_s2), .S3(adder_1_s3), .S4(adder_1_s4), .Cin(adapter_1_cin));
  // _74157 74157_1: pin names not known; wires that end beside it: adapter_1_mux, n7408_1_p3, adder_1_s1, S1, n7408_1_p6, adder_1_s2, S2, 1'b0, 1'b1, 1'b0, n7408_1_p14, adder_1_s4, S, n7408_1_p11, adder_1_s3, S3
  // _7486 7486_2: pin names not known; wires that end beside it: S, C, V, 1'b0, 1'b1
  // _7432 7432_1: pin names not known; wires that end beside it: S3, S, n7432_1_p3, n7432_1_p3, S2, n7432_1_p6, 1'b0, 1'b1, S1, n7432_1_p6, n7432_1_p11
  // _7404 7404_1: pin names not known; wires that end beside it: n7432_1_p11, Z, 1'b0, 1'b1

  assign S4 = S;
endmodule

module Adapter (
  input  cs2,
  input  cs1,
  input  cs0,
  output Cin,
  output MUX,
  output s1,
  output s0,
  output A_prime
);

  wire n7404_1_p2, n7404_1_p4, n7404_1_p6, n7404_1_p9, n7404_1_p10, n7408_1_p3, n7408_1_p6, n7408_1_p14,
       n7408_2_p5;

  // _7404 7404_1: pin names not known; wires that end beside it: cs0, n7404_1_p2, cs1, n7404_1_p4, cs2, n7404_1_p6, 1'b0, 1'b1, n7404_1_p9, n7404_1_p10
  // _7408 7408_1: pin names not known; wires that end beside it: cs0, n7404_1_p10, n7408_1_p3, n7404_1_p2, cs1, n7408_1_p6, 1'b0, 1'b1, cs0, cs2, A_prime, n7404_1_p6, cs1, n7408_1_p14
  // _7432 7432_1: pin names not known; wires that end beside it: cs1, cs2, n7404_1_p9, n7408_1_p3, n7408_1_p6, s1, 1'b0, 1'b1, cs0, cs1, MUX, n7404_1_p2, n7408_1_p14, s0
  // _7408 7408_2: pin names not known; wires that end beside it: 1'b0, 1'b1, cs0, n7404_1_p6, n7408_2_p5
  // _7432 7432_2: pin names not known; wires that end beside it: 1'b0, 1'b1, n7404_1_p4, n7408_2_p5, Cin
endmodule

module FA_Extender (
  input  B,
  input  s1,
  input  s0,
  output B_2
);

  wire n7404_1_p4, n7408_1_p3, n7408_1_p8;

  // _7404 7404_1: pin names not known; wires that end beside it: 1'b0, 1'b1, B, n7404_1_p4
  // _7408 7408_1: pin names not known; wires that end beside it: n7404_1_p4, s1, n7408_1_p3, 1'b0, 1'b1, B, s0, n7408_1_p8
  // _7432 7432_1: pin names not known; wires that end beside it: n7408_1_p3, n7408_1_p8, B_2, 1'b0, 1'b1
endmodule

module Adder (
  input  Cin,
  input  A1,
  input  A2,
  input  A3,
  input  A4,
  input  B1,
  input  B2,
  input  B3,
  input  B4,
  output Cout,
  output S1,
  output S2,
  output S3,
  output S4
);

  // _7483 7483_1: pin names not known; wires that end beside it: A4, S3, A3, B3, 1'b1, S2, B2, A2, B4, S4, Cout, Cin, 1'b0, B1, A1, S1
endmodule
