// Logisim project FPA.circ as structural Verilog: 4 circuits, main circuit main
module main (
  input  [21:0] in_1
);

  wire normalize_1_p2, normalize_1_p3, normalize_1_p4;

  // Normalize normalize_1: pin names not known; wires that end beside it: in_1, normalize_1_p2, normalize_1_p3, normalize_1_p4
endmodule

module Normalize (
  input  [11:0] Exp,
  input  [24:0] IN,
  output [11:0] Exponent,
  output [4:0] Shifted_amount,
  output [24:0] Fraction,
  output All_zero
);

  wire bitfinder_1_found;
  wire [11:0] adder_1_out;

  Adder #(.width(12)) adder_1 (.a(Exp), .b(12'h1), .out(adder_1_out));  // open: cin, cout
  BitFinder #(.width(25)) bitfinder_1 (
    .in({IN[0], IN[1], IN[2], IN[3], IN[4], IN[5], IN[6], IN[7], IN[8], IN[9], IN[10], IN[11], IN[12], IN[13], IN[14], IN[15], IN[16], IN[17], IN[18], IN[19], IN[20], IN[21], IN[22], IN[23], IN[24]}),
    .index(Shifted_amount), .found(bitfinder_1_found));
  Shifter #(.width(25)) shifter_1 (.in(IN), .\dist (Shifted_amount), .out(Fraction));
  Subtractor #(.width(12)) subtractor_1 (
    .a(adder_1_out), .b({{7{1'b0}}, Shifted_amount}), .out(Exponent));  // open: bin, bout
  not not_1 (All_zero, bitfinder_1_found);
endmodule

module Complement (
  input  [24:0] in_1,
  output [24:0] out_2,
  output out_3
);

  wire [24:0] negator_1_out;

  Negator #(.width(25)) negator_1 (.in(in_1), .out(negator_1_out));
  Multiplexer #(.width(25), .disabled(0), .enable("false")) multiplexer_1 (
    .in0(in_1), .in1(negator_1_out), .out(out_2), .sel(in_1[24]));

  assign out_3 = in_1[24];
endmodule

module Rounding (
  input  [24:0] in_1,
  output [24:0] Result
);

  wire or_1_out;
  wire [24:0] adder_1_out, multiplexer_1_out;

  Adder #(.width(25)) adder_1 (.a(in_1), .b(25'h8), .out(adder_1_out));  // open: cin, cout
  or or_1 (or_1_out, in_1[0], in_1[1]);
  Multiplexer #(.width(25), .enable("false")) multiplexer_1 (
    .in0({in_1[24:4], 4'b0000}), .in1({adder_1_out[24:3], 3'b000}), .out(multiplexer_1_out), .sel(or_1_out));
  Multiplexer #(.width(25), .enable("false")) multiplexer_2 (
    .in0(in_1), .in1(multiplexer_1_out), .out(Result), .sel(in_1[2]));
endmodule
