// Logisim project FPA_main.circ as structural Verilog: 5 circuits, main circuit Full_Adder
module Full_Adder (
  input  [31:0] A,
  input  [31:0] B,
  output [11:0] out_3,
  output [24:0] Smaller,
  output [24:0] Larger,
  output [11:0] Larger_Exp,
  output [24:0] Shifted_Smaller,
  output [24:0] Fractions_Sum,
  output [24:0] Fraction,
  output [11:0] Exponent,
  output [31:0] Output
);

  wire Compare_Exp_x____y, Compare_Exp_x___y, complement_1_out_3;
  wire [4:0] Compare31_out_2;
  wire [11:0] normalize_1_exponent, Split_Input_2_exponent, Split_Input_exponent;
  wire [24:0] complement_1_out_2, normalize_1_fraction, rounding_1_result,
       Split_Input_2_sign_adjusted_fraction, Split_Input_sign_adjusted_fraction;

  SplitInput Split_Input (
    .A(A), .Exponent(Split_Input_exponent), .Sign_adjusted_Fraction(Split_Input_sign_adjusted_fraction));  // open: Sign_Bit
  My_Comparator Compare_Exp (
    .X(Split_Input_exponent), .Y(Split_Input_2_exponent), .X____Y(Compare_Exp_x____y),
    .X___Y(Compare_Exp_x___y), .Difference(out_3), .Larger(Larger_Exp));  // open: out_6
  Compare31 Compare31 (.in_1(out_3), .out_2(Compare31_out_2));
  Combine combine_1 (.in_1(Fraction), .Exponent(Exponent), .Sign_Bit(complement_1_out_3), .out_4(Output));
  Multiplexer #(.width(25), .disabled(0), .enable("false")) multiplexer_1 (
    .in0(Split_Input_sign_adjusted_fraction), .in1(Split_Input_2_sign_adjusted_fraction), .out(Smaller),
    .sel(Compare_Exp_x____y));
  Shifter #(.width(25), .shift("ar")) shifter_1 (.in(Smaller), .\dist (Compare31_out_2), .out(Shifted_Smaller));
  Multiplexer #(.width(25), .disabled(0), .enable("false")) multiplexer_2 (
    .in0(Split_Input_sign_adjusted_fraction), .in1(Split_Input_2_sign_adjusted_fraction), .out(Larger),
    .sel(Compare_Exp_x___y));
  SplitInput Split_Input_2 (
    .A(B), .Exponent(Split_Input_2_exponent), .Sign_adjusted_Fraction(Split_Input_2_sign_adjusted_fraction));  // open: Sign_Bit
  Adder #(.width(25)) adder_1 (.a(Larger), .b(Shifted_Smaller), .out(Fractions_Sum), .cin(1'b0));  // open: cout
  Complement complement_1 (.in_1(Fractions_Sum), .out_2(complement_1_out_2), .out_3(complement_1_out_3));
  Normalize normalize_1 (
    .Exp(Larger_Exp), .IN(complement_1_out_2), .Exponent(normalize_1_exponent),
    .Fraction(normalize_1_fraction));  // open: Shifted_amount, All_zero
  Rounding rounding_1 (.in_1(normalize_1_fraction), .Result(rounding_1_result));
  Normalize normalize_2 (
    .Exp(normalize_1_exponent), .IN(rounding_1_result), .Exponent(Exponent), .Fraction(Fraction));  // open: Shifted_amount, All_zero
endmodule

module SplitInput (
  input  [31:0] A,
  output Sign_Bit,
  output [11:0] Exponent,
  output [24:0] Sign_adjusted_Fraction
);

  wire [24:0] negator_1_out;

  Negator #(.width(25)) negator_1 (.in({3'b001, A[18:0], 3'b000}), .out(negator_1_out));
  Multiplexer #(.width(25), .enable("false")) multiplexer_1 (
    .in0({3'b001, A[18:0], 3'b000}), .in1(negator_1_out), .out(Sign_adjusted_Fraction), .sel(A[31]));

  assign Exponent = A[30:19];
  assign Sign_Bit = A[31];
endmodule

module My_Comparator (
  input  [11:0] X,
  input  [11:0] Y,
  output X____Y,
  output X___Y,
  output [11:0] Difference,
  output out_6,
  output [11:0] Larger
);

  wire comparator_1_eq, comparator_1_gt;
  wire [11:0] multiplexer_1_out;

  Comparator #(.width(12), .mode("unsigned")) comparator_1 (
    .a(X), .b(Y), .gt(comparator_1_gt), .eq(comparator_1_eq), .lt(X___Y));
  or or_1 (X____Y, comparator_1_gt, comparator_1_eq);
  Multiplexer #(.width(12), .disabled(0), .enable("false")) multiplexer_1 (
    .in0(X), .in1(Y), .out(multiplexer_1_out), .sel(X____Y));
  Multiplexer #(.width(12), .disabled(0), .enable("false")) multiplexer_2 (.in0(X), .in1(Y), .out(Larger), .sel(X___Y));
  Subtractor #(.width(12)) subtractor_1 (.a(Larger), .b(multiplexer_1_out), .out(Difference), .bin(1'b0), .bout(out_6));

  // Notes on the sheet:
  //   Smaller
  //   Larger
endmodule

module Compare31 (
  input  [11:0] in_1,
  output [4:0] out_2
);

  wire comparator_1_lt;
  wire [11:5] multiplexer_1_out;

  Comparator #(.width(12), .mode("unsigned")) comparator_1 (
    .a(in_1), .b(12'h1f), .lt(comparator_1_lt));  // open: gt, eq
  Multiplexer #(.width(12), .enable("false")) multiplexer_1 (
    .in0(12'h1f), .in1(in_1), .out({multiplexer_1_out, out_2}), .sel(comparator_1_lt));
endmodule

module Combine (
  input  [24:0] in_1,
  input  [11:0] Exponent,
  input  Sign_Bit,
  output [31:0] out_4
);


  assign out_4 = {Sign_Bit, Exponent, in_1[23:5]};
endmodule
