// Logisim project Control Unit.circ as structural Verilog: 1 circuit, main circuit main
module main (
  input  [3:0] Op_Code,
  output RegDst,
  output Jump,
  output Beq,
  output Bneq,
  output MemRead,
  output MemToReg,
  output [2:0] ALUOp,
  output MemWrite,
  output ALUSrc,
  output RegWrite
);

  ROM #(.addrWidth(4), .dataWidth(12)) rom_1 (
    .addr(Op_Code), .data({RegWrite, ALUSrc, MemWrite, ALUOp, MemToReg, MemRead, Bneq, Beq, Jump, RegDst}));  // open: sel
  // Probe on {RegWrite, ALUSrc, MemWrite, ALUOp, MemToReg, MemRead, Bneq, Beq, Jump, RegDst}

  // Notes on the sheet:
  //   contents of rom_1 (hex, n*v repeats v):
  //   2 48 841 801 c00 d40 cc0 8c1 44 c30 901 881 d80 c40 c80 600
endmodule
