// Logisim project Data_Memory.circ as structural Verilog: 1 circuit, main circuit Data_Memory
module Data_Memory (
  input  [3:0] Address,
  input  [3:0] Write_Dta,
  input  MemWrite,
  input  Clk,
  input  MemRead,
  output [3:0] Output
);

  wire not_1_out;

  not not_1 (not_1_out, Clk);
  RAM #(.addrWidth(4), .dataWidth(4), .bus("separate")) ram_1 (
    .addr(Address), .din(Write_Dta), .data(Output), .str(MemWrite), .clk(not_1_out), .ld(MemRead));  // open: sel, clr
endmodule
