// Logisim project Instruction.circ as structural Verilog: 1 circuit, main circuit main
module main (
  input  [7:0] Read_Address,
  output [15:0] Instruction
);

  ROM #(.dataWidth(16)) rom_1 (.addr(Read_Address), .data(Instruction));  // open: sel

  // Notes on the sheet:
  //   contents of rom_1 (hex, n*v repeats v):
  //   4713 d72e 3120 2123 a024 f213 c221 8321 120 5331 9224 110 7020 e421 6115 b241 120 120a
endmodule
