// Logisim project MIPS_Final (1).circ as structural Verilog: 1 circuit, main circuit main
module main (
  output [3:0] t0,
  output [3:0] t1,
  output [3:0] t2,
  output [3:0] t3,
  output [3:0] t4,
  output [7:0] Current_PC,
  output [15:0] Instruction,
  output [3:0] Read_Data2,
  output [3:0] Read_Data1,
  output [3:0] Alu_Output,
  output [3:0] Data_Read
);

  wire ALU_zero, CLK_out, Control_Unit_alusrc, Control_Unit_beq, Control_Unit_bneq, Control_Unit_jump,
       Control_Unit_memread, Control_Unit_memtoreg, Control_Unit_memwrite, Control_Unit_regdst,
       Control_Unit_regwrite, For_beq_out, For_bneq_out, not_1_out, or_1_out;
  wire [2:0] Control_Unit_aluop;
  wire [3:0] multiplexer_1_out, multiplexer_2_out, multiplexer_4_out;
  wire [7:0] adder_1_out, adder_2_out, bit_extender_1_out, multiplexer_3_out, multiplexer_5_out;

  Register #(.trigger("falling")) PC (.D(multiplexer_5_out), .Q(Current_PC), .clk(CLK_out), .clr(1'b0));  // open: en
  Clock CLK (.out(CLK_out));
  Instruction_main u_Instruction (.Read_Address(Current_PC), .Instruction(Instruction));
  Control_Unit_main Control_Unit (
    .Op_Code(Instruction[15:12]), .RegDst(Control_Unit_regdst), .Jump(Control_Unit_jump),
    .Beq(Control_Unit_beq), .Bneq(Control_Unit_bneq), .MemRead(Control_Unit_memread),
    .MemToReg(Control_Unit_memtoreg), .ALUOp(Control_Unit_aluop), .MemWrite(Control_Unit_memwrite),
    .ALUSrc(Control_Unit_alusrc), .RegWrite(Control_Unit_regwrite));
  Multiplexer #(.width(4), .enable("false")) multiplexer_1 (
    .in0(Instruction[7:4]), .in1(Instruction[3:0]), .out(multiplexer_1_out), .sel(Control_Unit_regdst));
  Adder adder_1 (.a(Current_PC), .b(8'h1), .out(adder_1_out));  // open: cin, cout
  Register_Memory register_memory_1 (
    .SrcReg1(Instruction[11:8]), .Write_Data(multiplexer_4_out), .RegWrite(Control_Unit_regwrite),
    .CLK(CLK_out), .DstReg1(multiplexer_1_out), .SrcReg2(Instruction[7:4]), .Read_1_Data(Read_Data1),
    .Read_2_Data(Read_Data2), .registers_state({t4, t3, t2, t1, t0}));
  assign bit_extender_1_out = {{4{Instruction[3]}}, Instruction[3:0]};  // Bit_Extender bit_extender_1
  Multiplexer #(.width(4), .enable("false")) multiplexer_2 (
    .in0(Read_Data2), .in1(Instruction[3:0]), .out(multiplexer_2_out), .sel(Control_Unit_alusrc));
  Adder adder_2 (.a(adder_1_out), .b(bit_extender_1_out), .out(adder_2_out));  // open: cin, cout
  Main ALU (
    .Input_1(Read_Data1), .Input_2(multiplexer_2_out), .ALUOp(Control_Unit_aluop), .Zero(ALU_zero),
    .Output(Alu_Output));  // open: Overflow
  not not_1 (not_1_out, ALU_zero);
  and For_beq (For_beq_out, Control_Unit_beq, ALU_zero);
  and For_bneq (For_bneq_out, Control_Unit_bneq, not_1_out);
  Data_Memory Data_Memory (
    .Address(Alu_Output), .Write_Dta(Read_Data2), .MemWrite(Control_Unit_memwrite), .Clk(CLK_out),
    .MemRead(Control_Unit_memread), .Output(Data_Read));
  Multiplexer #(.width(8), .enable("false")) multiplexer_3 (
    .in0(adder_1_out), .in1(adder_2_out), .out(multiplexer_3_out), .sel(or_1_out));
  or or_1 (or_1_out, For_beq_out, For_bneq_out);
  Multiplexer #(.width(4), .enable("false")) multiplexer_4 (
    .in0(Alu_Output), .in1(Data_Read), .out(multiplexer_4_out), .sel(Control_Unit_memtoreg));
  Multiplexer #(.width(8), .enable("false")) multiplexer_5 (
    .in0(multiplexer_3_out), .in1(Instruction[11:4]), .out(multiplexer_5_out), .sel(Control_Unit_jump));
endmodule
