// Logisim project Main-Alu.circ as structural Verilog: 8 circuits, main circuit Add
module Add (
  input  [3:0] X,
  input  [3:0] Y,
  output [3:0] Result,
  output Overflow
);

  wire adder_1_cout, adder_2_cout;

  Adder #(.width(3)) adder_1 (.a(X[2:0]), .b(Y[2:0]), .out(Result[2:0]), .cout(adder_1_cout));  // open: cin
  Adder #(.width(1)) adder_2 (.a(X[3]), .b(Y[3]), .out(Result[3]), .cin(adder_1_cout), .cout(adder_2_cout));
  xor xor_1 (Overflow, adder_1_cout, adder_2_cout);
endmodule

// sub
module Sub (
  input  [3:0] X,
  input  [3:0] Y,
  output Zero,
  output [3:0] Output,
  output Overflow
);

  wire [3:0] negator_1_out;

  Negator #(.width(4)) negator_1 (.in(Y), .out(negator_1_out));
  Add add_1 (.X(X), .Y(negator_1_out), .Result(Output), .Overflow(Overflow));
  nor nor_1 (Zero, Output[0], Output[1], Output[2], Output[3]);
endmodule

// and
module And (
  input  [3:0] X,
  input  [3:0] Y,
  output [3:0] Output
);

  assign Output = X & Y;  // AND_Gate and_1, 4 bits wide
endmodule

// or
module Or (
  input  [3:0] X,
  input  [3:0] y,
  output [3:0] Result
);

  assign Result = X | y;  // OR_Gate or_1, 4 bits wide
endmodule

// nor
module Nor (
  input  [3:0] X,
  input  [3:0] y,
  output [3:0] X_2
);

  assign X_2 = ~(X | y);  // NOR_Gate nor_1, 4 bits wide
endmodule

// sll
module Sll (
  input  [3:0] X,
  input  [3:0] Y,
  output [3:0] Result
);

  Shifter #(.width(4)) shifter_1 (.in(X), .\dist (Y[1:0]), .out(Result));
endmodule

// srl
module Srl (
  input  [3:0] X,
  input  [3:0] Y,
  output [3:0] Result
);

  Shifter #(.width(4), .shift("ar")) shifter_1 (.in(X), .\dist (Y[1:0]), .out(Result));
endmodule

module Main (
  input  [3:0] Input_1,
  input  [3:0] Input_2,
  input  [2:0] ALUOp,
  output Overflow,
  output Zero,
  output [3:0] Output
);

  wire add_1_overflow, sub_1_overflow;
  wire [3:0] add_1_result, and_1_output, nor_1_x_2, or_1_result, sll_1_result, srl_1_result, sub_1_output;

  Add add_1 (.X(Input_1), .Y(Input_2), .Result(add_1_result), .Overflow(add_1_overflow));
  Sub sub_1 (.X(Input_1), .Y(Input_2), .Zero(Zero), .Output(sub_1_output), .Overflow(sub_1_overflow));
  And and_1 (.X(Input_1), .Y(Input_2), .Output(and_1_output));
  Or or_1 (.X(Input_1), .y(Input_2), .Result(or_1_result));
  Nor nor_1 (.X(Input_1), .y(Input_2), .X_2(nor_1_x_2));
  Sll sll_1 (.X(Input_1), .Y(Input_2), .Result(sll_1_result));
  Srl srl_1 (.X(Input_1), .Y(Input_2), .Result(srl_1_result));
  Multiplexer #(.select(3), .enable("false")) multiplexer_1 (
    .in0(add_1_overflow), .in1(sub_1_overflow), .in2(1'b0), .in3(1'b0), .in4(1'b0), .in5(1'b0), .in6(1'b0),
    .in7(1'b0), .out(Overflow), .sel(ALUOp));
  Multiplexer #(.select(3), .width(4), .enable("false")) multiplexer_2 (
    .in0(add_1_result), .in1(sub_1_output), .in2(and_1_output), .in3(or_1_result), .in4(nor_1_x_2),
    .in5(sll_1_result), .in6(srl_1_result), .out(Output), .sel(ALUOp));  // open: in7
endmodule
