// Logisim project Register_Memory.circ as structural Verilog: 1 circuit, main circuit Register Memory
module Register_Memory (
  input  [3:0] SrcReg1,
  input  [3:0] Write_Data,
  input  RegWrite,
  input  CLK,
  input  [3:0] DstReg1,
  input  [3:0] SrcReg2,
  output [19:0] registers_state,
  output [3:0] Read_1_Data,
  output [3:0] Read_2_Data
);

  wire and_1_out, demultiplexer_1_out0, demultiplexer_1_out1, demultiplexer_1_out2, demultiplexer_1_out3,
       demultiplexer_1_out4, not_1_out, not_2_out, not_3_out, not_4_out, not_5_out;
  wire [3:0] zero_q;

  and and_1 (and_1_out, RegWrite, CLK);
  Demultiplexer #(.select(3), .enable("false")) demultiplexer_1 (
    .out0(demultiplexer_1_out0), .out1(demultiplexer_1_out1), .out2(demultiplexer_1_out2),
    .out3(demultiplexer_1_out3), .out4(demultiplexer_1_out4), .in(and_1_out), .sel(DstReg1[2:0]));  // open: out5, out6, out7
  Register #(.width(4)) zero (.D(4'b0000), .Q(zero_q), .clk(1'b0));  // open: en, clr
  Register #(.width(4)) t0 (.D(Write_Data), .Q(registers_state[3:0]), .clk(not_1_out));  // open: en, clr
  not not_1 (not_1_out, demultiplexer_1_out0);
  Register #(.width(4)) t1 (.D(Write_Data), .Q(registers_state[7:4]), .clk(not_2_out));  // open: en, clr
  not not_2 (not_2_out, demultiplexer_1_out1);
  Register #(.width(4)) t2 (.D(Write_Data), .Q(registers_state[11:8]), .clk(not_3_out));  // open: en, clr
  not not_3 (not_3_out, demultiplexer_1_out2);
  Register #(.width(4)) t3 (.D(Write_Data), .Q(registers_state[15:12]), .clk(not_4_out));  // open: en, clr
  not not_4 (not_4_out, demultiplexer_1_out3);
  Register #(.width(4)) t4 (.D(Write_Data), .Q(registers_state[19:16]), .clk(not_5_out));  // open: en, clr
  not not_5 (not_5_out, demultiplexer_1_out4);
  Multiplexer #(.select(3), .width(4), .enable("false")) multiplexer_1 (
    .in0(registers_state[3:0]), .in1(registers_state[7:4]), .in2(registers_state[11:8]),
    .in3(registers_state[15:12]), .in4(registers_state[19:16]), .in7(zero_q), .out(Read_1_Data),
    .sel(SrcReg1[2:0]));  // open: in5, in6
  Multiplexer #(.select(3), .width(4), .enable("false")) multiplexer_2 (
    .in0(registers_state[3:0]), .in1(registers_state[7:4]), .in2(registers_state[11:8]),
    .in3(registers_state[15:12]), .in4(registers_state[19:16]), .in7(zero_q), .out(Read_2_Data),
    .sel(SrcReg2[2:0]));  // open: in5, in6
endmodule
